// Logisim project alternate-mutually-exclusive-switch-bank_LtoH.circ as structural Verilog: 1 circuit, main circuit main
module main (
);

  wire and_1_out, and_2_out, and_3_out, and_4_out, button_1_out, button_2_out, button_3_out, button_4_out,
       d_ff_1_q, d_ff_1_qn, d_ff_2_q, d_ff_2_qn, d_ff_3_q, d_ff_3_qn, d_ff_4_q, d_ff_4_qn, or_1_out,
       or_2_out, or_3_out, or_4_out, or_5_out;

  Button button_1 (.out(button_1_out));
  Button button_2 (.out(button_2_out));
  Button button_3 (.out(button_3_out));
  Button button_4 (.out(button_4_out));
  or or_1 (or_1_out, button_1_out, button_2_out, button_3_out, button_4_out);
  and and_1 (and_1_out, d_ff_1_q, or_1_out);
  or or_2 (or_2_out, and_1_out, button_1_out);
  and and_2 (and_2_out, d_ff_2_q, or_1_out);
  or or_3 (or_3_out, and_2_out, button_2_out);
  and and_3 (and_3_out, d_ff_3_q, or_1_out);
  or or_4 (or_4_out, and_3_out, button_3_out);
  and and_4 (and_4_out, d_ff_4_q, or_1_out);
  or or_5 (or_5_out, and_4_out, button_4_out);
  D_Flip_Flop d_ff_1 (.clk(or_2_out), .D(d_ff_1_qn), .Q(d_ff_1_q), .Qn(d_ff_1_qn));  // open: preset, en, reset
  D_Flip_Flop d_ff_2 (.clk(or_3_out), .D(d_ff_2_qn), .Q(d_ff_2_q), .Qn(d_ff_2_qn));  // open: preset, en, reset
  D_Flip_Flop d_ff_3 (.clk(or_4_out), .D(d_ff_3_qn), .Q(d_ff_3_q), .Qn(d_ff_3_qn));  // open: preset, en, reset
  D_Flip_Flop d_ff_4 (.clk(or_5_out), .D(d_ff_4_qn), .Q(d_ff_4_q), .Qn(d_ff_4_qn));  // open: preset, en, reset
  LED led_1 (.in(d_ff_1_q));
  LED led_2 (.in(d_ff_2_q));
  LED led_3 (.in(d_ff_3_q));
  LED led_4 (.in(d_ff_4_q));
endmodule
