// Logisim project maintained-mutually-exclusive-switch-bank_HtoL-8.circ as structural Verilog: 1 circuit, main circuit main
module main (
);

  wire button_1_out, button_2_out, button_3_out, button_4_out, button_5_out, button_6_out, button_7_out,
       button_8_out, d_ff_1_qn, d_ff_2_qn, d_ff_3_qn, d_ff_4_qn, d_ff_5_qn, d_ff_6_qn, d_ff_7_qn, d_ff_8_qn,
       nand_1_out, nand_2_out, not_1_out, not_2_out, not_3_out, not_4_out, not_5_out, not_6_out, not_7_out,
       not_8_out, or_1_out;

  Button button_1 (.out(button_1_out));
  Button button_2 (.out(button_2_out));
  Button button_3 (.out(button_3_out));
  Button button_4 (.out(button_4_out));
  Button button_5 (.out(button_5_out));
  Button button_6 (.out(button_6_out));
  Button button_7 (.out(button_7_out));
  Button button_8 (.out(button_8_out));
  not not_1 (not_1_out, button_1_out);
  not not_2 (not_2_out, button_2_out);
  not not_3 (not_3_out, button_3_out);
  not not_4 (not_4_out, button_4_out);
  not not_5 (not_5_out, button_5_out);
  not not_6 (not_6_out, button_6_out);
  not not_7 (not_7_out, button_7_out);
  not not_8 (not_8_out, button_8_out);
  nand nand_1 (nand_1_out, not_1_out, not_2_out, not_3_out, not_4_out);
  nand nand_2 (nand_2_out, not_5_out, not_6_out, not_7_out, not_8_out);
  or or_1 (or_1_out, nand_1_out, nand_2_out);
  D_Flip_Flop d_ff_1 (.clk(or_1_out), .D(not_1_out), .Qn(d_ff_1_qn));  // open: Q, preset, en, reset
  D_Flip_Flop d_ff_2 (.clk(or_1_out), .D(not_2_out), .Qn(d_ff_2_qn));  // open: Q, preset, en, reset
  D_Flip_Flop d_ff_3 (.clk(or_1_out), .D(not_3_out), .Qn(d_ff_3_qn));  // open: Q, preset, en, reset
  D_Flip_Flop d_ff_4 (.clk(or_1_out), .D(not_4_out), .Qn(d_ff_4_qn));  // open: Q, preset, en, reset
  D_Flip_Flop d_ff_5 (.clk(or_1_out), .D(not_5_out), .Qn(d_ff_5_qn));  // open: Q, preset, en, reset
  D_Flip_Flop d_ff_6 (.clk(or_1_out), .D(not_6_out), .Qn(d_ff_6_qn));  // open: Q, preset, en, reset
  D_Flip_Flop d_ff_7 (.clk(or_1_out), .D(not_7_out), .Qn(d_ff_7_qn));  // open: Q, preset, en, reset
  D_Flip_Flop d_ff_8 (.clk(or_1_out), .D(not_8_out), .Qn(d_ff_8_qn));  // open: Q, preset, en, reset
  LED led_1 (.in(d_ff_1_qn));
  LED led_2 (.in(d_ff_2_qn));
  LED led_3 (.in(d_ff_3_qn));
  LED led_4 (.in(d_ff_4_qn));
  LED led_5 (.in(d_ff_5_qn));
  LED led_6 (.in(d_ff_6_qn));
  LED led_7 (.in(d_ff_7_qn));
  LED led_8 (.in(d_ff_8_qn));
endmodule
