// Logisim project maintained-mutually-exclusive-switch-bank_LtoH.circ as structural Verilog: 1 circuit, main circuit main
module main (
);

  wire button_1_out, button_2_out, button_3_out, button_4_out, d_ff_1_q, d_ff_2_q, d_ff_3_q, d_ff_4_q,
       or_1_out;

  Button button_1 (.out(button_1_out));
  Button button_2 (.out(button_2_out));
  Button button_3 (.out(button_3_out));
  Button button_4 (.out(button_4_out));
  or or_1 (or_1_out, button_1_out, button_2_out, button_3_out, button_4_out);
  D_Flip_Flop d_ff_1 (.clk(or_1_out), .D(button_1_out), .Q(d_ff_1_q));  // open: Qn, preset, en, reset
  D_Flip_Flop d_ff_2 (.clk(or_1_out), .D(button_2_out), .Q(d_ff_2_q));  // open: Qn, preset, en, reset
  D_Flip_Flop d_ff_3 (.clk(or_1_out), .D(button_3_out), .Q(d_ff_3_q));  // open: Qn, preset, en, reset
  D_Flip_Flop d_ff_4 (.clk(or_1_out), .D(button_4_out), .Q(d_ff_4_q));  // open: Qn, preset, en, reset
  LED led_1 (.in(d_ff_1_q));
  LED led_2 (.in(d_ff_2_q));
  LED led_3 (.in(d_ff_3_q));
  LED led_4 (.in(d_ff_4_q));

  // Notes on the sheet:
  //   maintained mutually-exclusive switch-bank
endmodule
